// Logisim project Guia_06.circ as structural Verilog: 4 circuits, main circuit Guia_0605
module Guia_0605 (
  input  x,
  input  z,
  input  y,
  output s
);

  wire and_1_out, and_2_out, not_1_out, not_2_out;

  not not_1 (not_1_out, x);
  not not_2 (not_2_out, z);
  and and_1 (and_1_out, not_1_out, y);
  or or_1 (s, and_1_out, and_2_out);
  and and_2 (and_2_out, not_2_out, y);

  // Notes on the sheet:
  //   Expressão Simplificada: ~x & y    +   y & ~z
endmodule

module Guia_0606 (
  input  X,
  input  W,
  input  Y,
  input  Z,
  output S
);

  wire not_1_out, not_2_out, not_3_out, not_4_out, not_5_out, or_1_out, or_2_out;

  not not_1 (not_1_out, Y);
  not not_2 (not_2_out, W);
  not not_3 (not_3_out, Z);
  not not_4 (not_4_out, X);
  not not_5 (not_5_out, Y);
  or or_1 (or_1_out, not_1_out, not_2_out, not_3_out);
  or or_2 (or_2_out, not_4_out, W, not_5_out, Z);
  and and_1 (S, or_1_out, or_2_out);

  // Notes on the sheet:
  //   Expressão Simplificada: Y'+W'+Z' . X'+Y'+W+Z
endmodule

module Guia_0607 (
  input  X,
  input  Y,
  input  Z,
  output S
);

  wire not_1_out, not_2_out, or_1_out, or_2_out;

  not not_1 (not_1_out, Y);
  not not_2 (not_2_out, X);
  or or_1 (or_1_out, X, not_1_out, Z);
  or or_2 (or_2_out, not_2_out, Y, Z);
  and and_1 (S, or_1_out, or_2_out);

  // Notes on the sheet:
  //   Expressão Simplificada: X' + Y + Z  . X + Y' +Z
endmodule

module Guia_0608 (
  input  x,
  input  w,
  input  y,
  input  z,
  output s
);

  wire and_1_out, and_2_out, and_3_out, not_1_out, not_2_out, not_3_out, not_4_out, not_5_out;

  and and_1 (and_1_out, x, w, z);
  not not_1 (not_1_out, x);
  and and_2 (and_2_out, w, not_1_out, not_2_out, z);
  not not_2 (not_2_out, y);
  not not_3 (not_3_out, x);
  not not_4 (not_4_out, w);
  and and_3 (and_3_out, not_3_out, not_4_out, not_5_out, y);
  not not_5 (not_5_out, z);
  or or_1 (s, and_1_out, and_2_out, and_3_out);

  // Notes on the sheet:
  //   Expressão Simplificada: x.w.z + w.x'.y'.z + w'.x'.y.z'
endmodule
