// Logisim project Atividade01.circ as structural Verilog: 5 circuits, main circuit half_adder
module half_adder (
  input  x0,
  input  y0,
  output s0,
  output c_out
);

  xor xor_1 (s0, x0, y0);
  and and_1 (c_out, x0, y0);
endmodule

module somador1bit (
  input  cin,
  input  x1,
  input  y1,
  output s1,
  output c_out
);

  wire half_adder_1_c_out, half_adder_1_s0, half_adder_2_c_out;

  half_adder half_adder_1 (.x0(x1), .y0(y1), .c_out(half_adder_1_c_out), .s0(half_adder_1_s0));
  half_adder half_adder_2 (.x0(cin), .y0(half_adder_1_s0), .c_out(half_adder_2_c_out), .s0(s1));
  or or_1 (c_out, half_adder_1_c_out, half_adder_2_c_out);
endmodule

module full_adder4bits (
  input  cin,
  input  x0,
  input  y0,
  input  x1,
  input  y1,
  input  x2,
  input  y2,
  input  x3,
  input  y3,
  output s0,
  output s1,
  output s2,
  output s3,
  output c_out
);

  wire somador1bit_1_c_out, somador1bit_2_c_out, somador1bit_3_c_out;

  somador1bit somador1bit_1 (.x1(x0), .y1(y0), .cin(cin), .c_out(somador1bit_1_c_out), .s1(s0));
  somador1bit somador1bit_2 (.x1(x1), .y1(y1), .cin(somador1bit_1_c_out), .c_out(somador1bit_2_c_out), .s1(s1));
  somador1bit somador1bit_3 (.x1(x2), .y1(y2), .cin(somador1bit_2_c_out), .c_out(somador1bit_3_c_out), .s1(s2));
  somador1bit somador1bit_4 (.x1(x3), .y1(y3), .cin(somador1bit_3_c_out), .c_out(c_out), .s1(s3));
endmodule

module main (
  input  in_1,
  input  in_2,
  input  in_3,
  input  in_4,
  input  in_5,
  input  in_6,
  input  in_7,
  input  in_8,
  input  in_9,
  input  in_10,
  input  in_11,
  input  in_12,
  input  in_13,
  output out_14,
  output out_15,
  output out_16,
  output out_17,
  output out_18
);

  wire decodificador_1_a, decodificador_1_b, decodificador_1_c, decodificador_1_d, decodificador_1_e,
       decodificador_1_f, decodificador_1_g, decodificador_2_a, decodificador_2_b;

  decodificador decodificador_1 (
    .e3(in_1), .e2(in_3), .e1(in_4), .e0(in_5), .a(decodificador_1_a), .b(decodificador_1_b),
    .c(decodificador_1_c), .d(decodificador_1_d), .e(decodificador_1_e), .f(decodificador_1_f),
    .g(decodificador_1_g));
  decodificador decodificador_2 (
    .e3(in_10), .e2(in_11), .e1(in_12), .e0(in_13), .a(decodificador_2_a), .b(decodificador_2_b));  // open: c, d, e, f, g
  _7_Segment_Display u_7_segment_display_1 (
    .g(decodificador_1_g), .f(decodificador_1_f), .a(decodificador_1_a), .b(decodificador_1_b),
    .e(decodificador_1_d), .d(decodificador_1_e), .c(decodificador_1_c));  // open: dp
  full_adder4bits full_adder4bits_1 (
    .x0(in_1), .y0(in_6), .x1(in_3), .y1(in_7), .x2(in_4), .y2(in_8), .x3(in_5), .y3(in_9), .cin(in_2),
    .c_out(out_18), .s0(out_14), .s1(out_15), .s2(out_16), .s3(out_17));
  _7_Segment_Display u_7_segment_display_2 (.a(decodificador_2_b), .b(decodificador_2_a));  // open: g, f, e, d, c, dp
endmodule

module decodificador (
  input  e3,
  input  e2,
  input  e1,
  input  e0,
  output a,
  output b,
  output c,
  output d,
  output e,
  output f,
  output g
);

  wire and_1_out, and_2_out, and_3_out, and_4_out, and_5_out, and_6_out, and_7_out, and_8_out, and_9_out,
       and_10_out, and_11_out, and_12_out, and_13_out, and_14_out, and_15_out, and_16_out, and_17_out,
       and_18_out, and_19_out, and_20_out, and_21_out, and_22_out, and_23_out, and_24_out, and_25_out,
       and_26_out, and_27_out, and_28_out, and_29_out, and_30_out, and_31_out, and_32_out, and_33_out,
       and_34_out, and_35_out, not_1_out, not_2_out, not_3_out, not_4_out, not_5_out, not_6_out, not_7_out,
       not_8_out, not_9_out, not_10_out, not_11_out, not_12_out, not_13_out, not_14_out, not_15_out,
       not_16_out, not_17_out, not_18_out, not_19_out, not_20_out, not_21_out, not_22_out, not_23_out,
       not_24_out, not_25_out, not_26_out, not_27_out, not_28_out, not_29_out, not_30_out, not_31_out,
       not_32_out, not_33_out, not_34_out, not_35_out, not_36_out, not_37_out, not_38_out, not_39_out,
       not_40_out, not_41_out, not_42_out, not_43_out, not_44_out;

  not not_1 (not_1_out, e2);
  and and_1 (and_1_out, not_1_out, not_2_out);
  not not_2 (not_2_out, e0);
  not not_3 (not_3_out, e3);
  and and_2 (and_2_out, not_3_out, e1);
  not not_4 (not_4_out, e3);
  and and_3 (and_3_out, not_4_out, e2, e0);
  and and_4 (and_4_out, e2, e1);
  and and_5 (and_5_out, e3, not_5_out, not_6_out);
  not not_5 (not_5_out, e2);
  not not_6 (not_6_out, e1);
  and and_6 (and_6_out, e3, not_7_out);
  not not_7 (not_7_out, e0);
  not not_8 (not_8_out, e3);
  and and_7 (and_7_out, not_8_out, not_9_out);
  not not_9 (not_9_out, e2);
  not not_10 (not_10_out, e3);
  not not_11 (not_11_out, e1);
  and and_8 (and_8_out, not_10_out, not_11_out, not_12_out);
  not not_12 (not_12_out, e0);
  not not_13 (not_13_out, e2);
  and and_9 (and_9_out, not_13_out, not_14_out);
  not not_14 (not_14_out, e0);
  not not_15 (not_15_out, e3);
  and and_10 (and_10_out, not_15_out, e1, e0);
  and and_11 (and_11_out, e3, not_16_out, e0);
  not not_16 (not_16_out, e1);
  not not_17 (not_17_out, e3);
  and and_12 (and_12_out, not_17_out, not_18_out);
  not not_18 (not_18_out, e1);
  not not_19 (not_19_out, e3);
  and and_13 (and_13_out, not_19_out, e0);
  not not_20 (not_20_out, e1);
  and and_14 (and_14_out, not_20_out, e0);
  not not_21 (not_21_out, e3);
  and and_15 (and_15_out, not_21_out, e2);
  and and_16 (and_16_out, e3, not_22_out);
  not not_22 (not_22_out, e2);
  not not_23 (not_23_out, e2);
  and and_17 (and_17_out, not_23_out, not_24_out);
  not not_24 (not_24_out, e0);
  not not_25 (not_25_out, e2);
  and and_18 (and_18_out, not_25_out, e1);
  and and_19 (and_19_out, e1, not_26_out);
  not not_26 (not_26_out, e0);
  not not_27 (not_27_out, e1);
  and and_20 (and_20_out, e2, not_27_out, e0);
  and and_21 (and_21_out, e3, not_28_out);
  not not_28 (not_28_out, e1);
  not not_29 (not_29_out, e2);
  and and_22 (and_22_out, not_29_out, not_30_out);
  not not_30 (not_30_out, e0);
  and and_23 (and_23_out, e1, not_31_out);
  not not_31 (not_31_out, e0);
  and and_24 (and_24_out, e3, e1);
  and and_25 (and_25_out, e3, e2);
  not not_32 (not_32_out, e1);
  and and_26 (and_26_out, not_32_out, not_33_out);
  not not_33 (not_33_out, e0);
  not not_34 (not_34_out, e3);
  and and_27 (and_27_out, not_34_out, e2, not_35_out);
  not not_35 (not_35_out, e1);
  and and_28 (and_28_out, e2, not_36_out);
  not not_36 (not_36_out, e0);
  and and_29 (and_29_out, e3, not_37_out);
  not not_37 (not_37_out, e2);
  and and_30 (and_30_out, e3, e1);
  not not_38 (not_38_out, e3);
  and and_31 (and_31_out, not_38_out, not_39_out, e1);
  not not_39 (not_39_out, e2);
  not not_40 (not_40_out, e3);
  and and_32 (and_32_out, not_40_out, e2, not_41_out);
  not not_41 (not_41_out, e1);
  and and_33 (and_33_out, e2, e1, not_42_out);
  not not_42 (not_42_out, e0);
  not not_43 (not_43_out, e2);
  and and_34 (and_34_out, e3, not_43_out, not_44_out);
  not not_44 (not_44_out, e1);
  and and_35 (and_35_out, e3, e0);
  or or_1 (b, and_7_out, and_8_out, and_9_out, and_10_out, and_11_out);
  or or_2 (c, and_12_out, and_13_out, and_14_out, and_15_out, and_16_out);
  or or_3 (d, and_17_out, and_18_out, and_19_out, and_20_out, and_21_out);
  or or_4 (e, and_22_out, and_23_out, and_24_out, and_25_out);
  or or_5 (f, and_26_out, and_27_out, and_28_out, and_29_out, and_30_out);
  or or_6 (g, and_31_out, and_32_out, and_33_out, and_34_out, and_35_out);
  or or_7 (a, and_1_out, and_2_out, and_3_out, and_4_out, and_5_out, and_6_out);
endmodule
