// Logisim project Guia03_C2.circ as structural Verilog: 1 circuit, main circuit main
module main (
  input  A,
  input  B,
  input  C,
  output Soma,
  output out_5
);

  wire and_1_out, and_2_out, or_1_out;

  or or_1 (or_1_out, A, B);
  or or_2 (Soma, or_1_out, C);
  and and_1 (and_1_out, or_1_out, C);
  and and_2 (and_2_out, A, B);
  or or_3 (out_5, and_1_out, and_2_out);
endmodule
