// Logisim project Guia0402.circ as structural Verilog: 1 circuit, main circuit main
module main (
  input  x,
  input  nx,
  input  nx_2,
  input  ny,
  input  y,
  input  nx_3,
  input  x_2,
  input  nx_4,
  input  y_2,
  input  y_3,
  input  y_4,
  input  nx_5,
  input  y_5,
  input  y_6,
  input  nx_6,
  input  x_3,
  input  ny_2,
  input  x_4,
  input  y_7,
  output sa,
  output sc,
  output sb,
  output se,
  output sd
);

  wire and_2_out, and_3_out, and_5_out, not_1_out, not_2_out, not_3_out, not_4_out, not_5_out, not_6_out,
       not_7_out, not_8_out, not_9_out, not_10_out, not_11_out, not_12_out, not_13_out, or_1_out, or_2_out,
       or_4_out, or_6_out, or_7_out, or_8_out;

  not not_1 (not_1_out, nx_3);
  not not_2 (not_2_out, nx_5);
  not not_3 (not_3_out, x_3);
  and and_1 (sa, x, not_4_out);
  or or_1 (or_1_out, not_1_out, y_2);
  not not_4 (not_4_out, or_1_out);
  and and_2 (and_2_out, not_2_out, y_6);
  or or_2 (or_2_out, not_3_out, y_7);
  not not_5 (not_5_out, and_2_out);
  or or_3 (sd, not_5_out, or_2_out);
  not not_6 (not_6_out, nx_2);
  not not_7 (not_7_out, nx_4);
  or or_4 (or_4_out, not_6_out, y);
  or or_5 (sb, or_4_out, and_3_out);
  and and_3 (and_3_out, not_7_out, y_4);
  or or_6 (or_6_out, y_5, not_8_out);
  not not_8 (not_8_out, nx_6);
  not not_9 (not_9_out, ny_2);
  or or_7 (or_7_out, not_9_out, x_4);
  and and_4 (se, or_6_out, not_10_out);
  not not_10 (not_10_out, or_7_out);
  not not_11 (not_11_out, nx);
  not not_12 (not_12_out, ny);
  and and_5 (and_5_out, not_11_out, not_12_out);
  not not_13 (not_13_out, and_5_out);
  or or_8 (or_8_out, x_2, y_3);
  and and_6 (sc, not_13_out, or_8_out);

  // Notes on the sheet:
  //   02.)
  //   a.) x.(x' + y)'
  //   d.) ( x' . y )' + ( x' + y)
  //   b) ( x' + y ) + ( x' . y )
  //   e.) ( y + x' ) . ( y' + x )' 
  //   c.) ( x' . y' )' . ( x + y ) 
endmodule
