// Logisim project Guia0500.circ as structural Verilog: 5 circuits, main circuit Guia0501
module Guia0501 (
  input  a,
  input  b,
  input  in_3,
  input  in_4,
  output out_5,
  output out_6
);

  wire nor_2_out, not_out;

  not \not  (not_out, a);
  and and_1 (out_5, not_out, b);
  nor nor_1 (out_6, in_3, nor_2_out);
  nor nor_2 (nor_2_out, in_4, in_4);

  // Notes on the sheet:
  //   Original
  //   Usando portas NOR
endmodule

module Guia0502 (
  input  Original,
  input  in_2,
  input  in_3,
  input  in_4,
  output out_5,
  output out_6
);

  wire nand_1_out, not_1_out;

  or or_1 (out_5, Original, not_1_out);
  not not_1 (not_1_out, in_2);
  nand nand_1 (nand_1_out, in_3, in_3);
  nand nand_2 (out_6, nand_1_out, in_4);

  // Notes on the sheet:
  //   Usando portas NAND
endmodule

module Guia0503 (
  input  a,
  input  b,
  input  a_2,
  input  b_2,
  output s,
  output s_2
);

  wire nor_1_out, not_1_out, or_1_out;

  not not_1 (not_1_out, a);
  or or_1 (or_1_out, not_1_out, b);
  nor nor_1 (nor_1_out, a_2, a_2);
  not not_2 (s, or_1_out);
  nor nor_2 (s_2, nor_1_out, b_2);

  // Notes on the sheet:
  //   Original
  //   Usando Portas NOR
endmodule

module Guia0504 (
  input  a,
  input  b,
  input  a_2,
  input  b_2,
  output s,
  output s_2
);

  wire and_1_out, nand_1_out, not_out;

  not \not  (not_out, a);
  and and_1 (and_1_out, not_out, b);
  nand nand_1 (nand_1_out, a_2, a_2);
  not not_2 (s, and_1_out);
  nand nand_2 (s_2, nand_1_out, b_2);

  // Notes on the sheet:
  //   Original
  //   Usando Portas NAND
endmodule

module Guia0506 (
  input  in_1,
  input  in_2,
  output out_3,
  output out_4
);

  wire and_1_out;

  and and_1 (and_1_out, in_1, in_2);
  not not_1 (out_3, and_1_out);
  xnor xnor_1 (out_4, in_1, in_2);
endmodule
