// Logisim project Guia_07.circ as structural Verilog: 5 circuits, main circuit Guia_0701
module Guia_0701 (
  input  a,
  input  select,
  input  b,
  input  a_2,
  input  select_2,
  input  b_2,
  output out_7,
  output s
);

  wire and_1_out, and_2_out, nand1_out, nand2_out, nand3_out, not_out;

  nand nand1 (nand1_out, select, select);
  not \not  (not_out, select_2);
  and and_1 (and_1_out, a_2, not_out);
  and and_2 (and_2_out, select_2, b_2);
  nand nand3 (nand3_out, a, nand1_out);
  nand nand2 (nand2_out, select, b);
  or or1 (s, and_1_out, and_2_out);
  nand nand4 (out_7, nand3_out, nand2_out);

  // Notes on the sheet:
  //   sa
  //   sb
  //   sel
endmodule

module Guia_0702 (
  input  a,
  input  sel,
  input  b,
  output out_4
);

  wire nor1_out, nor2_out, nor3_out, or1_out;

  nor nor2 (nor2_out, sel, sel);
  nor nor3 (nor3_out, nor2_out, b);
  nor nor1 (nor1_out, a, sel);
  or or1 (or1_out, nor3_out, nor3_out);
  nor nor4 (out_4, nor1_out, or1_out);

  // Notes on the sheet:
  //   w1
  //   sa
  //   sb
  //   w2
endmodule

module Guia_0703 (
  input  a,
  input  b,
  input  sel1,
  input  sel2,
  output s1,
  output s2
);

  wire nand1_out, nand2_out, nand3_out, nor1_out, nor2_out, nor3_out, or1_out;

  nand nand1 (nand1_out, sel1, sel1);
  nor nor1 (nor1_out, sel2, sel2);
  nand nand2 (nand2_out, nand1_out, a);
  nor nor2 (nor2_out, sel2, a);
  nand nand3 (nand3_out, sel1, b);
  nor nor3 (nor3_out, nor1_out, b);
  or or1 (or1_out, nor3_out, nor3_out);
  nand nand4 (s1, nand2_out, nand3_out);
  nor nor4 (s2, nor2_out, or1_out);

  // Notes on the sheet:
  //   w4
  //   w1
  //   w6
  //   w3
  //   w5
  //   w2
  //   w7
endmodule

module Guia_0704 (
  input  in_1,
  input  in_2,
  input  [1:0] in_3,
  output out_4
);

  wire nor_1_out, or_1_out, xnor_1_out;

  or or_1 (or_1_out, in_2, in_1);
  xor xor_1 (or_1_out, in_1, in_2);
  nor nor_1 (nor_1_out, in_1, in_2);
  xnor xnor_1 (xnor_1_out, in_1, in_2);
  Multiplexer #(.select(2), .enable("false")) multiplexer_1 (
    .in0(or_1_out), .in1(or_1_out), .in2(nor_1_out), .in3(xnor_1_out), .out(out_4), .sel(in_3));
endmodule

module Guia_0705 (
  input  in_1,
  input  in_2,
  input  [2:0] in_3,
  output out_4
);

  wire and_1_out, nand_1_out, nor_1_out, not_1_out, not_2_out, or_1_out, xnor_1_out, xor_1_out;

  not not_1 (not_1_out, in_1);
  not not_2 (not_2_out, in_2);
  and and_1 (and_1_out, in_1, in_2);
  nand nand_1 (nand_1_out, in_1, in_2);
  or or_1 (or_1_out, in_1, in_1);
  nor nor_1 (nor_1_out, in_1, in_2);
  xor xor_1 (xor_1_out, in_1, in_2);
  xnor xnor_1 (xnor_1_out, in_1, in_2);
  Multiplexer #(.select(3), .enable("false")) multiplexer_1 (
    .in0(not_1_out), .in1(not_2_out), .in2(and_1_out), .in3(nand_1_out), .in4(or_1_out), .in5(nor_1_out),
    .in6(xor_1_out), .in7(xnor_1_out), .out(out_4), .sel(in_3));
endmodule
