// Logisim project Guia_08.circ as structural Verilog: 13 circuits, main circuit half_adder
module half_adder (
  input  x,
  input  y,
  output s0,
  output s1
);

  xor xor_1 (s0, x, y);
  and and_1 (s1, x, y);
endmodule

// +
module full_adder (
  input  x,
  input  y,
  input  vai_um,
  output s0,
  output s1
);

  wire half_adder_1_s0, half_adder_1_s1, half_adder_2_s1;

  half_adder half_adder_1 (.s0(half_adder_1_s0), .s1(half_adder_1_s1), .x(x), .y(y));
  half_adder half_adder_2 (.s0(s0), .s1(half_adder_2_s1), .x(vai_um), .y(half_adder_1_s0));
  or or_1 (s1, half_adder_2_s1, half_adder_1_s1);
endmodule

module half_difference (
  input  x,
  input  y,
  output s0,
  output s1
);

  wire not_1_out;

  xor xor_1 (s0, x, y);
  not not_1 (not_1_out, x);
  and and_1 (s1, not_1_out, y);
endmodule

// |
module full_diference (
  input  x,
  input  y,
  input  vem_um,
  output s0,
  output s1
);

  wire half_difference_1_s0, half_difference_1_s1, half_difference_2_s1;

  half_difference half_difference_1 (.s0(half_difference_1_s0), .s1(half_difference_1_s1), .x(x), .y(y));
  half_difference half_difference_2 (.s0(s0), .s1(half_difference_2_s1), .x(half_difference_1_s0), .y(vem_um));
  or or_1 (s1, half_difference_2_s1, half_difference_1_s1);
endmodule

module comparador (
  input  in_1,
  input  in_2,
  input  in_3,
  input  in_4,
  input  in_5,
  input  in_6,
  input  in_7,
  input  in_8,
  input  B,
  input  in_10,
  input  in_11,
  input  in_12,
  output s5,
  output s4,
  output s3,
  output s2,
  output s1,
  output s0
);

  xor xor_1 (s5, in_1, in_7);
  xor xor_2 (s4, in_2, in_8);
  xor xor_3 (s3, in_3, B);
  xor xor_4 (s2, in_4, in_10);
  xor xor_5 (s1, in_5, in_11);
  xor xor_6 (s0, in_6, in_12);

  // Notes on the sheet:
  //   A
endmodule

module mux (
  input  a,
  input  select,
  input  b,
  output s
);

  wire and_1_out, and_2_out, not_out;

  not \not  (not_out, select);
  and and_1 (and_1_out, a, not_out);
  and and_2 (and_2_out, select, b);
  or or1 (s, and_1_out, and_2_out);

  // Notes on the sheet:
  //   sa
  //   sb
endmodule

module Guia_801 (
  input  sinal,
  input  in_2,
  input  in_3,
  input  in_4,
  input  in_5,
  input  sinal_2,
  input  in_7,
  input  in_8,
  input  in_9,
  input  in_10,
  input  cin,
  output cout,
  output s4,
  output s3,
  output s2,
  output s1,
  output s0
);

  wire full_adder_2_s1, full_adder_3_s1, full_adder_4_s1, full_adder_5_s1;

  full_adder full_adder_1 (.s0(s4), .s1(cout), .x(sinal), .y(sinal_2), .vai_um(full_adder_2_s1));
  full_adder full_adder_2 (.s0(s3), .s1(full_adder_2_s1), .x(in_2), .y(in_7), .vai_um(full_adder_3_s1));
  full_adder full_adder_3 (.s0(s2), .s1(full_adder_3_s1), .x(in_3), .y(in_8), .vai_um(full_adder_4_s1));
  full_adder full_adder_4 (.s0(s1), .s1(full_adder_4_s1), .x(in_4), .y(in_9), .vai_um(full_adder_5_s1));
  full_adder full_adder_5 (.s0(s0), .s1(full_adder_5_s1), .x(in_5), .y(in_5), .vai_um(cin));

  assign in_10 = in_5;
endmodule

module Guia_0802 (
  input  sinal,
  input  in_2,
  input  in_3,
  input  in_4,
  input  in_5,
  input  sinal_2,
  input  in_7,
  input  in_8,
  input  in_9,
  input  in_10,
  input  cin,
  output cout,
  output s4,
  output s3,
  output s2,
  output s1,
  output s0
);

  wire full_diference_2_s0, full_diference_3_s1, full_diference_4_s1, full_diference_5_s0;

  full_diference full_diference_1 (.x(sinal), .y(sinal_2), .vem_um(full_diference_2_s0), .s0(cout), .s1(s4));
  full_diference full_diference_2 (.x(in_2), .y(in_7), .vem_um(full_diference_3_s1), .s0(full_diference_2_s0), .s1(s3));
  full_diference full_diference_3 (.x(in_3), .y(in_8), .vem_um(full_diference_5_s0), .s0(s2), .s1(full_diference_3_s1));
  full_diference full_diference_4 (.x(in_5), .y(in_10), .vem_um(cin), .s0(s0), .s1(full_diference_4_s1));
  full_diference full_diference_5 (.x(in_4), .y(in_9), .vem_um(full_diference_4_s1), .s0(full_diference_5_s0), .s1(s1));
endmodule

module Guia_0803 (
  input  sinal,
  input  in_2,
  input  in_3,
  input  in_4,
  input  in_5,
  input  sinal_2,
  input  in_7,
  input  in_8,
  input  in_9,
  input  in_10,
  input  cin,
  output cout,
  output s3,
  output s2,
  output s1,
  output s0,
  output s4,
  output out_18
);

  wire full_diference_2_s0, full_diference_3_s1, full_diference_4_s0, full_diference_5_s1;

  full_diference full_diference_1 (.x(sinal), .y(sinal_2), .vem_um(full_diference_2_s0), .s0(cout), .s1(s4));
  full_diference full_diference_2 (.x(in_2), .y(in_7), .vem_um(full_diference_3_s1), .s0(full_diference_2_s0), .s1(s3));
  NotExactlyOne xnor_1 (.out(out_18), .in0(s4), .in1(s3), .in2(s2), .in3(s1), .in4(s0));
  full_diference full_diference_3 (.x(in_3), .y(in_8), .vem_um(full_diference_4_s0), .s0(s2), .s1(full_diference_3_s1));
  full_diference full_diference_4 (.x(in_4), .y(in_9), .vem_um(full_diference_5_s1), .s0(full_diference_4_s0), .s1(s1));
  full_diference full_diference_5 (.x(in_5), .y(in_10), .vem_um(cin), .s0(s0), .s1(full_diference_5_s1));
endmodule

module Guia_0804 (
  input  in_1,
  input  in_2,
  input  in_3,
  input  in_4,
  input  in_5,
  input  in_6,
  input  in_7,
  input  in_8,
  input  in_9,
  input  in_10,
  input  carry_in,
  output carry_out,
  output s4,
  output s3,
  output s2,
  output s1,
  output s0,
  output out_18
);

  wire full_diference_2_s0, full_diference_3_s0, full_diference_4_s0, full_diference_5_s0;

  full_diference full_diference_1 (.x(in_1), .y(in_6), .vem_um(full_diference_2_s0), .s0(carry_out), .s1(s4));
  full_diference full_diference_2 (.x(in_2), .y(in_7), .vem_um(full_diference_3_s0), .s0(full_diference_2_s0), .s1(s3));
  ExactlyOne \xor  (.out(out_18), .in0(s4), .in1(s3), .in2(s2), .in3(s1), .in4(s0));
  full_diference full_diference_3 (.x(in_3), .y(in_8), .vem_um(full_diference_4_s0), .s0(full_diference_3_s0), .s1(s2));
  full_diference full_diference_4 (.x(in_4), .y(in_9), .vem_um(full_diference_5_s0), .s0(full_diference_4_s0), .s1(s1));
  full_diference full_diference_5 (.x(in_5), .y(in_10), .vem_um(carry_in), .s0(full_diference_5_s0), .s1(s0));
endmodule

module Guia_0805 (
  input  A5,
  input  A4,
  input  A3,
  input  A2,
  input  A1,
  input  A0,
  input  carry_in,
  output carry_out,
  output s5,
  output s4,
  output s3,
  output s2,
  output s1,
  output s0
);

  wire half_adder_2_s1, half_adder_3_s1, half_adder_4_s1, half_adder_5_s1, half_adder_6_s1, not_1_out,
       not_2_out, not_3_out, not_4_out, not_5_out, not_6_out;

  not not_1 (not_1_out, A4);
  not not_2 (not_2_out, A5);
  half_adder half_adder_1 (.s0(s5), .s1(carry_out), .x(half_adder_2_s1), .y(not_2_out));
  not not_3 (not_3_out, A3);
  half_adder half_adder_2 (.s0(s4), .s1(half_adder_2_s1), .x(half_adder_3_s1), .y(not_1_out));
  half_adder half_adder_3 (.s0(s3), .s1(half_adder_3_s1), .x(half_adder_5_s1), .y(not_3_out));
  not not_4 (not_4_out, A2);
  not not_5 (not_5_out, A1);
  half_adder half_adder_4 (.s0(s1), .s1(half_adder_4_s1), .x(half_adder_6_s1), .y(not_5_out));
  half_adder half_adder_5 (.s0(s2), .s1(half_adder_5_s1), .x(half_adder_4_s1), .y(not_4_out));
  not not_6 (not_6_out, A0);
  half_adder half_adder_6 (.s0(s0), .s1(half_adder_6_s1), .x(carry_in), .y(not_6_out));
endmodule

module Guia_0806 (
  input  carry_in,
  input  in_2,
  input  in_3,
  input  in_4,
  input  in_5,
  input  in_6,
  input  in_7,
  input  in_8,
  input  in_9,
  input  B,
  input  in_11,
  input  in_12,
  input  in_13,
  input  in_14,
  output carry_out,
  output s5,
  output s4,
  output s3,
  output s2,
  output s1,
  output s0,
  output s_comp
);

  wire full_adder_2_s1, full_adder_3_s1, full_adder_4_s1, full_adder_5_s1, full_adder_6_s1, xnor_out,
       xor_1_out, xor_2_out, xor_3_out, xor_4_out, xor_5_out, xor_6_out, xor_7_out;

  full_adder full_adder_1 (.s0(s5), .s1(carry_out), .x(in_2), .y(xor_2_out), .vai_um(full_adder_2_s1));
  full_adder full_adder_2 (.s0(s4), .s1(full_adder_2_s1), .x(xor_1_out), .y(in_3), .vai_um(full_adder_3_s1));
  full_adder full_adder_3 (.s0(s3), .s1(full_adder_3_s1), .x(xor_3_out), .y(in_4), .vai_um(full_adder_4_s1));
  NotExactlyOne \xnor  (.out(xnor_out), .in0(s5), .in1(s4), .in2(s3), .in3(s2), .in4(s1), .in5(s0));
  xor xor_1 (xor_1_out, carry_in, in_9);
  xor xor_2 (xor_2_out, carry_in, in_8);
  full_adder full_adder_4 (.s0(s2), .s1(full_adder_4_s1), .x(xor_4_out), .y(in_5), .vai_um(full_adder_5_s1));
  mux mux_1 (.a(xor_5_out), .select(in_14), .b(xnor_out), .s(s_comp));
  xor xor_3 (xor_3_out, carry_in, B);
  xor xor_4 (xor_4_out, carry_in, in_11);
  full_adder full_adder_5 (.s0(s1), .s1(full_adder_5_s1), .x(xor_7_out), .y(in_6), .vai_um(full_adder_6_s1));
  ExactlyOne xor_5 (.out(xor_5_out), .in0(s5), .in1(s4), .in2(s3), .in3(s2), .in4(s1), .in5(s0));
  xor xor_6 (xor_6_out, carry_in, in_13);
  xor xor_7 (xor_7_out, carry_in, in_12);
  full_adder full_adder_6 (.s0(s0), .s1(full_adder_6_s1), .x(xor_6_out), .y(in_7), .vai_um(carry_in));

  // Notes on the sheet:
  //   A
  //   mux
endmodule

module Guia_0807 (
  input  in_1,
  input  in_2,
  input  in_3,
  input  in_4,
  input  in_5,
  input  in_6,
  input  in_7,
  input  in_8,
  input  in_9,
  input  in_10,
  input  in_11,
  input  in_12,
  input  chave,
  output s
);

  wire comparador_1_s0, comparador_1_s1, comparador_1_s2, comparador_1_s3, comparador_1_s4, comparador_1_s5,
       not_1_out, or_1_out;

  comparador comparador_1 (
    .in_1(in_1), .in_2(in_2), .in_3(in_3), .in_4(in_4), .in_5(in_5), .in_6(in_6), .in_7(in_7), .in_8(in_8),
    .B(in_9), .in_10(in_10), .in_11(in_11), .in_12(in_12), .s5(comparador_1_s5), .s4(comparador_1_s4),
    .s3(comparador_1_s3), .s2(comparador_1_s2), .s1(comparador_1_s1), .s0(comparador_1_s0));
  or or_1 (or_1_out, comparador_1_s5, comparador_1_s4, comparador_1_s3, comparador_1_s2, comparador_1_s1, comparador_1_s0);
  not not_1 (not_1_out, or_1_out);
  mux mux_1 (.a(not_1_out), .select(chave), .b(or_1_out), .s(s));

  // Notes on the sheet:
  //   A
  //   comparador
  //   mux
  //   B
endmodule
