// Logisim project Preparacao_01.circ as structural Verilog: 10 circuits, main circuit P01a
module P01a (
  input  a,
  input  b,
  input  c,
  input  d,
  output out_5
);

  wire and_1_out, and_2_out, and_3_out, and_4_out, not_1_out, not_2_out, not_3_out, not_4_out, or_1_out,
       or_2_out;

  not not_1 (not_1_out, a);
  not not_2 (not_2_out, c);
  not not_3 (not_3_out, b);
  not not_4 (not_4_out, d);
  and and_1 (and_1_out, a, not_3_out, c, not_4_out);
  and and_2 (and_2_out, a, not_3_out, c, d);
  and and_3 (and_3_out, a, b, not_2_out, not_4_out);
  and and_4 (and_4_out, a, b, not_2_out, d);
  or or_1 (or_1_out, and_1_out, and_2_out);
  or or_2 (or_2_out, and_3_out, and_4_out);
  or or_3 (out_5, or_1_out, or_2_out);

  // Notes on the sheet:
  //   SoP Canonica
  //   a.b'.c.d' + a.b'.c.d + a.b.c'.d' . a.b.c'.d
endmodule

module P01b (
  input  A,
  input  B,
  input  C,
  input  D,
  output out_5
);

  wire and_1_out, and_2_out, not_1_out, not_2_out, not_3_out, not_4_out, or_1_out, or_2_out, or_3_out,
       or_4_out;

  not not_1 (not_1_out, A);
  not not_2 (not_2_out, B);
  not not_3 (not_3_out, C);
  not not_4 (not_4_out, D);
  or or_1 (or_1_out, not_1_out, B, not_3_out, D);
  or or_2 (or_2_out, not_1_out, B, not_3_out, not_4_out);
  or or_3 (or_3_out, not_1_out, not_2_out, C, D);
  or or_4 (or_4_out, not_1_out, not_2_out, C, not_4_out);
  and and_1 (and_1_out, or_1_out, or_2_out);
  and and_2 (and_2_out, or_3_out, or_4_out);
  and and_3 (out_5, and_1_out, and_2_out);

  // Notes on the sheet:
  //   PoS Canonica
  //   A'+B+C'+D . A'+B+C'+D' . A'+B'+C+D . A'+B'+C+D'
endmodule

module P01c (
  input  a,
  input  b,
  input  c,
  input  d,
  output out_5
);

  wire and_1_out, and_2_out, and_3_out, and_4_out, not_1_out, not_2_out, not_3_out, not_4_out, or_1_out,
       or_2_out;

  not not_1 (not_1_out, a);
  not not_2 (not_2_out, b);
  not not_3 (not_3_out, c);
  not not_4 (not_4_out, d);
  and and_1 (and_1_out, b, not_3_out, not_4_out);
  and and_2 (and_2_out, not_1_out, not_2_out, c, not_4_out);
  and and_3 (and_3_out, not_1_out, b, c, d);
  and and_4 (and_4_out, a, not_2_out, c, d);
  or or_1 (or_1_out, and_1_out, and_2_out);
  or or_2 (or_2_out, and_3_out, and_4_out);
  or or_3 (out_5, or_1_out, or_2_out);

  // Notes on the sheet:
  //   SoP Simplificada: mintermos
  //   b.c'.d' + a'.b'.c.d' + a'.b.c.d + a.b'.c.d
endmodule

module P01d (
  input  A,
  input  B,
  input  C,
  input  D,
  output out_5
);

  wire and_1_out, and_2_out, not_1_out, not_2_out, not_3_out, not_4_out, or_1_out, or_2_out, or_3_out,
       or_4_out, or_5_out, or_6_out, or_7_out, or_8_out;

  not not_1 (not_1_out, A);
  not not_2 (not_2_out, C);
  not not_3 (not_3_out, B);
  not not_4 (not_4_out, D);
  or or_1 (or_1_out, C, not_4_out);
  or or_2 (or_2_out, A, B, C);
  or or_3 (or_3_out, not_1_out, B, C);
  or or_4 (or_4_out, not_1_out, not_3_out, not_2_out);
  or or_5 (or_5_out, not_1_out, not_2_out, D);
  or or_6 (or_6_out, A, B, not_4_out);
  or or_7 (or_7_out, not_1_out, not_3_out, not_4_out);
  or or_8 (or_8_out, not_3_out, not_2_out, D);
  and and_1 (and_1_out, or_1_out, or_3_out, or_4_out, or_2_out);
  and and_2 (and_2_out, or_5_out, or_6_out, or_7_out, or_8_out);
  and and_3 (out_5, and_1_out, and_2_out);

  // Notes on the sheet:
  //   PoS Simplificada -  MAXTERMOS
  //   C+D' . A+B+C . A'+B+C . A'+B'+C' . A'+C'+D . A+B+D' . A'+B'+D' . B'+C'+D
endmodule

module P01e (
  input  in_1,
  input  in_2,
  input  in_3,
  input  in_4,
  output out_5
);

  wire nand_1_out, nand_2_out, nand_3_out, nand_4_out, nand_5_out, nand_6_out, nand_7_out, nand_8_out,
       nand_9_out, nand_10_out, nand_11_out, nand_12_out;

  nand nand_1 (nand_1_out, in_1, in_1);
  nand nand_2 (nand_2_out, in_2, in_2);
  nand nand_3 (nand_3_out, in_3, in_3);
  nand nand_4 (nand_4_out, in_4, in_4);
  nand nand_5 (nand_5_out, nand_4_out, nand_3_out, in_2);
  nand nand_6 (nand_6_out, nand_1_out, nand_2_out, in_3, nand_4_out);
  nand nand_7 (nand_7_out, nand_1_out, in_2, in_3, in_4);
  nand nand_8 (nand_8_out, in_1, nand_2_out, in_3, in_4);
  nand nand_9 (nand_9_out, nand_5_out, nand_6_out);
  nand nand_10 (nand_10_out, nand_7_out, nand_8_out);
  nand nand_11 (nand_11_out, nand_9_out, nand_9_out);
  nand nand_12 (nand_12_out, nand_10_out, nand_10_out);
  nand nand_13 (out_5, nand_11_out, nand_12_out);

  // Notes on the sheet:
  //   b.c'.d' + a'.b'.c.d' + a'.b.c.d + a.b'.c.d
endmodule

module P01f (
  input  A,
  input  B,
  input  C,
  input  D,
  output out_5
);

  wire nor_1_out, nor_2_out, nor_3_out, nor_4_out, nor_5_out, nor_6_out, nor_7_out, nor_8_out, nor_9_out,
       nor_10_out, nor_11_out, nor_12_out;

  nor nor_1 (nor_1_out, A, A);
  nor nor_2 (nor_2_out, C, C);
  nor nor_3 (nor_3_out, B, B);
  nor nor_4 (nor_4_out, D, D);
  nor nor_5 (nor_5_out, C, nor_4_out);
  nor nor_6 (nor_6_out, nor_1_out, B, C);
  nor nor_7 (nor_7_out, A, B, C);
  nor nor_8 (nor_8_out, nor_1_out, nor_3_out, nor_2_out);
  nor nor_9 (nor_9_out, nor_1_out, nor_2_out, D);
  nor nor_10 (nor_10_out, A, B, nor_4_out);
  nor nor_11 (nor_11_out, nor_1_out, nor_3_out, nor_4_out);
  nor nor_12 (nor_12_out, nor_3_out, nor_2_out, D);
  nor nor_13 (out_5, nor_5_out, nor_6_out, nor_7_out, nor_8_out, nor_9_out, nor_10_out, nor_11_out, nor_12_out);

  // Notes on the sheet:
  //   C+D' . A+B+C . A'+B+C . A'+B'+C' . A'+C'+D . A+B+D' . A'+B'+D' . B'+C'+D
endmodule

module P02 (
  input  x,
  input  y,
  output s
);

  wire and_1_out, not_1_out, not_2_out, not_3_out, or_1_out;

  not not_1 (not_1_out, x);
  not not_2 (not_2_out, y);
  and and_1 (and_1_out, y, not_1_out);
  or or_1 (or_1_out, not_2_out, x);
  and and_2 (s, and_1_out, not_3_out);
  not not_3 (not_3_out, or_1_out);
endmodule

module P03 (
  input  a,
  input  b,
  input  c,
  output out_4
);

  wire mux_2_s, mux_s, not_1_out, not_2_out, not_3_out;

  not not_1 (not_1_out, a);
  not not_2 (not_2_out, b);
  mux mux (.a(b), .select(c), .b(a), .s(mux_s));
  mux mux_2 (.a(not_1_out), .select(c), .b(not_2_out), .s(mux_2_s));
  not not_3 (not_3_out, c);
  mux mux_3 (.a(mux_s), .select(not_3_out), .b(mux_2_s), .s(out_4));
endmodule

module mux (
  input  a,
  input  select,
  input  b,
  output s
);

  wire and_1_out, and_2_out, not_1_out;

  and and_1 (and_1_out, a, not_1_out);
  not not_1 (not_1_out, select);
  and and_2 (and_2_out, select, b);
  or or_1 (s, and_1_out, and_2_out);
endmodule

module P05 (
  input  in_1,
  input  in_2,
  output out_3
);

  wire nor_1_out, not_1_out, not_2_out, xor_1_out;

  not not_1 (not_1_out, in_1);
  not not_2 (not_2_out, in_2);
  xor xor_1 (xor_1_out, in_1, in_2);
  nor nor_1 (nor_1_out, not_1_out, not_2_out);
  nand nand_1 (out_3, xor_1_out, nor_1_out);
endmodule
